# Fritzing sketch Humidity-Relays (saved by Fritzing 0.9.3b)
circuit board: 6.25371cm x 4.50781cm
breadboards: 1

parts:
  Raspberry_Pi_1 = Raspberry Pi 3 [part_number=RPI-3-V1.2]
  J2 = AVR ISP 6 Pin [package=2x3_lock]
  R1 = Resistor [tolerance=±5% resistance=220 package=THT]
  TRRS1 = Audio Jack (TRRS) 3.5mm [part_number="LUMBERG JEITA RC-5325A" package="RC-5325A [SMD]"]
  J3 = AVR ISP 6 Pin [package=2x3_lock]

nets:
  N1: Raspberry_Pi_1.3v3, R1.Pin_1, TRRS1.RING2
  N2: Raspberry_Pi_1.GPIO4, R1.Pin_0, TRRS1.RING1
  N3: Raspberry_Pi_1.GND, J2.3, TRRS1.TIP, J3.3
  N4: Raspberry_Pi_1.GPIO6, J2.1
  N5: Raspberry_Pi_1.GPIO13, J2.2
  N6: Raspberry_Pi_1.GPIO19, J2.4
  N7: Raspberry_Pi_1.GPIO26, J2.6
  N8: Raspberry_Pi_1.GPIO21, J3.1
  N9: Raspberry_Pi_1.GPIO20, J3.2
  N10: Raspberry_Pi_1.GPIO16, J3.4
  N11: Raspberry_Pi_1.GPIO12, J3.6
  N12: Raspberry_Pi_1.5V, J2.5, J3.5

custom parts:
  Raspberry Pi 3: The RPi3, a faster version of the awesome Raspberry Pi 2 B ARM Board with 40 pin gpio. Ready for special Raspberry Pi B+ and RPi2 Hat (Hardware attached (on) top)
