# Fritzing sketch HumiditySensorBreakout (saved by Fritzing 0.9.3b)
circuit board: 4.87491cm x 1.79379cm
breadboards: 1

parts:
  TRRS1 = Audio Jack (TRRS) 3.5mm [part_number="LUMBERG JEITA RC-5325A" package="RC-5325A [SMD]"]
  RHT1 = Humidity and Temperature Sensor RHT03

nets:
  N1: TRRS1.TIP, RHT1.GND_2
  N2: TRRS1.SLEEVE, RHT1.Data-signal
  N3: TRRS1.RING2, RHT1.Vcc
